// Logisim project Button_Detector.circ as structural Verilog: 4 circuits, main circuit Debouncer
module Debouncer (
  input  InputDebouncer,
  input  clk,
  input  rst,
  output OutputDebouncer
);

  wire d_ff_1_q, d_ff_2_q, d_ff_3_q;

  D_Flip_Flop d_ff_1 (.D(InputDebouncer), .clk(clk), .Q(d_ff_1_q), .reset(rst));  // open: Qn, preset
  D_Flip_Flop d_ff_2 (.D(d_ff_1_q), .clk(clk), .Q(d_ff_2_q), .reset(rst));  // open: Qn, preset
  D_Flip_Flop d_ff_3 (.D(d_ff_2_q), .clk(clk), .Q(d_ff_3_q), .reset(rst));  // open: Qn, preset
  and and_1 (OutputDebouncer, d_ff_1_q, d_ff_2_q, d_ff_3_q);
endmodule

module Synchronizer (
  input  InputSynchronizer,
  input  clk,
  input  rst,
  output OutputSynchronizer
);

  wire d_ff_1_q;

  D_Flip_Flop d_ff_1 (.D(InputSynchronizer), .clk(clk), .Q(d_ff_1_q), .reset(rst));  // open: Qn, preset
  D_Flip_Flop d_ff_2 (.D(d_ff_1_q), .clk(clk), .Q(OutputSynchronizer), .reset(rst));  // open: Qn, preset
endmodule

module Rising_Edge_Detector (
  input  InputRisingEdgeDetector,
  input  clk,
  input  rst,
  output OutputRisingEdgeDetector
);

  wire d_ff_1_qn;

  D_Flip_Flop d_ff_1 (.D(InputRisingEdgeDetector), .clk(clk), .Qn(d_ff_1_qn), .reset(rst));  // open: Q, preset
  and and_1 (OutputRisingEdgeDetector, InputRisingEdgeDetector, d_ff_1_qn);
endmodule

module Push_Button (
  input  InputPushButton,
  input  clk,
  input  rst,
  output OutputPushButton
);

  wire debouncer_1_outputdebouncer, synchronizer_1_outputsynchronizer;

  Debouncer debouncer_1 (
    .InputDebouncer(InputPushButton), .clk(clk), .rst(rst), .OutputDebouncer(debouncer_1_outputdebouncer));
  Synchronizer synchronizer_1 (
    .InputSynchronizer(debouncer_1_outputdebouncer), .clk(clk), .rst(rst),
    .OutputSynchronizer(synchronizer_1_outputsynchronizer));
  Rising_Edge_Detector rising_edge_detector_1 (
    .InputRisingEdgeDetector(synchronizer_1_outputsynchronizer), .clk(clk), .rst(rst),
    .OutputRisingEdgeDetector(OutputPushButton));
endmodule
