// Logisim project BCD_doubleDabble.circ as structural Verilog: 4 circuits, main circuit is_bigger_than_4
module is_bigger_than_4 (
  input  [3:0] number,
  output is_bigger
);

  wire and_1_out, and_2_out;

  and and_1 (and_1_out, number[2], number[1]);
  and and_2 (and_2_out, number[2], number[0]);
  or or_1 (is_bigger, number[3], and_1_out, and_2_out);
endmodule

module slicer_DP (
  input  rst,
  input  IsLoading,
  input  IsShifting,
  input  clk,
  input  [15:0] num,
  input  IsInit,
  output IsGreaterThan4,
  output [3:0] Digit0,
  output [3:0] Digit1,
  output [3:0] Digit2,
  output [3:0] Digit3,
  output [3:0] Digit4
);

  wire is_bigger_than_4_1_is_bigger, is_bigger_than_4_2_is_bigger, is_bigger_than_4_3_is_bigger,
       is_bigger_than_4_4_is_bigger, is_bigger_than_4_5_is_bigger;
  wire [3:0] adder_1_out, adder_2_out, adder_3_out, adder_4_out, adder_5_out, multiplexer_2_out,
       multiplexer_3_out, multiplexer_4_out, multiplexer_5_out, multiplexer_6_out, multiplexer_7_out,
       multiplexer_8_out, multiplexer_9_out, multiplexer_10_out, multiplexer_11_out;
  wire [15:0] multiplexer_1_out, shift_register_1_p18;

  Multiplexer #(.width(16)) multiplexer_1 (
    .in0(shift_register_1_p18), .in1(num), .out(multiplexer_1_out), .sel(IsInit));
  Multiplexer #(.width(4)) multiplexer_2 (
    .in0(multiplexer_9_out), .in1(4'b0000), .out(multiplexer_2_out), .sel(IsInit));
  Multiplexer #(.width(4)) multiplexer_3 (
    .in0(multiplexer_11_out), .in1(4'b0000), .out(multiplexer_3_out), .sel(IsInit));
  Multiplexer #(.width(4)) multiplexer_4 (
    .in0(multiplexer_7_out), .in1(4'b0000), .out(multiplexer_4_out), .sel(IsInit));
  Multiplexer #(.width(4)) multiplexer_5 (
    .in0(multiplexer_10_out), .in1(4'b0000), .out(multiplexer_5_out), .sel(IsInit));
  Multiplexer #(.width(4)) multiplexer_6 (
    .in0(multiplexer_8_out), .in1(4'b0000), .out(multiplexer_6_out), .sel(IsInit));
  // Shift_Register #(.length(36)) shift_register_1: pin names not known; wires that end beside it: rst, IsLoading, IsShifting, clk, 1'b0, multiplexer_1_out[0], multiplexer_1_out[1], multiplexer_1_out[2], multiplexer_1_out[3], multiplexer_1_out[4], multiplexer_1_out[5], multiplexer_1_out[6], multiplexer_1_out[7], multiplexer_1_out[8], multiplexer_1_out[9], multiplexer_1_out[10], multiplexer_1_out[11], shift_register_1_p18[0], shift_register_1_p18[1], shift_register_1_p18[2], shift_register_1_p18[3], shift_register_1_p18[4], shift_register_1_p18[5], shift_register_1_p18[6], shift_register_1_p18[7], shift_register_1_p18[8], shift_register_1_p18[9], shift_register_1_p18[10], shift_register_1_p18[11]
  is_bigger_than_4 is_bigger_than_4_1 (.number(Digit2), .is_bigger(is_bigger_than_4_1_is_bigger));
  is_bigger_than_4 is_bigger_than_4_2 (.number(Digit4), .is_bigger(is_bigger_than_4_2_is_bigger));
  Multiplexer #(.width(4)) multiplexer_7 (
    .in0(Digit2), .in1(adder_1_out), .out(multiplexer_7_out), .sel(is_bigger_than_4_1_is_bigger));
  Adder #(.width(4)) adder_1 (.a(Digit2), .b(4'b0011), .out(adder_1_out));  // open: cin, cout
  Multiplexer #(.width(4)) multiplexer_8 (
    .in0(Digit4), .in1(adder_2_out), .out(multiplexer_8_out), .sel(is_bigger_than_4_2_is_bigger));
  Adder #(.width(4)) adder_2 (.a(Digit4), .b(4'b0011), .out(adder_2_out));  // open: cin, cout
  is_bigger_than_4 is_bigger_than_4_3 (.number(Digit0), .is_bigger(is_bigger_than_4_3_is_bigger));
  Multiplexer #(.width(4)) multiplexer_9 (
    .in0(Digit0), .in1(adder_3_out), .out(multiplexer_9_out), .sel(is_bigger_than_4_3_is_bigger));
  Adder #(.width(4)) adder_3 (.a(Digit0), .b(4'b0011), .out(adder_3_out));  // open: cin, cout
  is_bigger_than_4 is_bigger_than_4_4 (.number(Digit3), .is_bigger(is_bigger_than_4_4_is_bigger));
  Multiplexer #(.width(4)) multiplexer_10 (
    .in0(Digit3), .in1(adder_4_out), .out(multiplexer_10_out), .sel(is_bigger_than_4_4_is_bigger));
  Adder #(.width(4)) adder_4 (.a(Digit3), .b(4'b0011), .out(adder_4_out));  // open: cin, cout
  is_bigger_than_4 is_bigger_than_4_5 (.number(Digit1), .is_bigger(is_bigger_than_4_5_is_bigger));
  Multiplexer #(.width(4)) multiplexer_11 (
    .in0(Digit1), .in1(adder_5_out), .out(multiplexer_11_out), .sel(is_bigger_than_4_5_is_bigger));
  Adder #(.width(4)) adder_5 (.a(Digit1), .b(4'b0011), .out(adder_5_out));  // open: cin, cout
  or or_1 (IsGreaterThan4, is_bigger_than_4_3_is_bigger, is_bigger_than_4_5_is_bigger, is_bigger_than_4_1_is_bigger, is_bigger_than_4_4_is_bigger, is_bigger_than_4_2_is_bigger);
endmodule

module slicer_CU (
  input  rst,
  input  is_greater,
  input  clk,
  input  start,
  output isDone,
  output isLoad,
  output isShift,
  output isInit
);

  wire IsUpdated_q, multiplexer_1_out, multiplexer_2_out, multiplexer_3_out, nand_1_out, not_1_out,
       not_2_out, not_3_out;
  wire [2:0] multiplexer_4_out, multiplexer_5_out;
  wire [4:0] counter_1_q;

  Multiplexer multiplexer_1 (.in0(is_greater), .in1(IsUpdated_q), .out(multiplexer_1_out), .sel(isInit));
  T_Flip_Flop IsUpdated (.T(multiplexer_1_out), .clk(clk), .Q(IsUpdated_q), .reset(rst));  // open: Qn, preset
  not not_1 (not_1_out, IsUpdated_q);
  Multiplexer #(.select(2)) multiplexer_2 (
    .in0(not_2_out), .in1(start), .in2(1'b1), .in3(1'b1), .out(multiplexer_2_out), .sel(counter_1_q[1:0]));
  not not_2 (not_2_out, start);
  nand nand_1 (nand_1_out, is_greater, not_1_out);
  Multiplexer multiplexer_3 (.in0(nand_1_out), .in1(multiplexer_2_out), .out(multiplexer_3_out), .sel(counter_1_q[4]));
  Counter #(.max('h12), .width(5)) counter_1 (
    .load(rst), .up(1'b1), .count(multiplexer_3_out), .clk(clk), .D(5'b10001), .Q(counter_1_q));  // open: clr, carry
  Multiplexer #(.width(3)) multiplexer_4 (.in0(3'b001), .in1(3'b010), .out(multiplexer_4_out), .sel(nand_1_out));
  Multiplexer #(.select(2), .width(3)) multiplexer_5 (
    .in0(3'b000), .in1(3'b000), .in2(3'b101), .in3(3'b101), .out(multiplexer_5_out), .sel(counter_1_q[1:0]));
  Multiplexer #(.width(3)) multiplexer_6 (
    .in0(multiplexer_4_out), .in1(multiplexer_5_out), .out({isInit, isShift, isLoad}), .sel(counter_1_q[4]));
  not not_3 (not_3_out, counter_1_q[1]);
  and and_1 (isDone, not_3_out, counter_1_q[4]);
endmodule

module slicerDoubleDabble (
  input  rst,
  input  clk,
  input  start,
  input  [15:0] num,
  output isDone,
  output [3:0] Digit0,
  output [3:0] Digit1,
  output [3:0] Digit2,
  output [3:0] Digit3,
  output [3:0] Digit4
);

  wire slicer_cu_1_isinit, slicer_cu_1_isload, slicer_cu_1_isshift, slicer_dp_1_isgreaterthan4;

  slicer_CU slicer_cu_1 (
    .rst(rst), .is_greater(slicer_dp_1_isgreaterthan4), .clk(clk), .start(start), .isDone(isDone),
    .isLoad(slicer_cu_1_isload), .isShift(slicer_cu_1_isshift), .isInit(slicer_cu_1_isinit));
  slicer_DP slicer_dp_1 (
    .rst(rst), .IsLoading(slicer_cu_1_isload), .IsShifting(slicer_cu_1_isshift), .clk(clk), .num(num),
    .IsInit(slicer_cu_1_isinit), .IsGreaterThan4(slicer_dp_1_isgreaterthan4), .Digit0(Digit0),
    .Digit1(Digit1), .Digit2(Digit2), .Digit3(Digit3), .Digit4(Digit4));
endmodule
