// Logisim project SSD_Render.circ as structural Verilog: 4 circuits, main circuit seven_seg_decoder
module seven_seg_decoder (
  input  [3:0] input_4bit,
  output A,
  output B,
  output C,
  output D,
  output E,
  output F,
  output G
);

  wire and_1_out, and_2_out, and_3_out, and_4_out, and_5_out, and_6_out, and_7_out, and_8_out, and_9_out,
       and_10_out, and_11_out, and_12_out, and_13_out, not_1_out, not_2_out, not_3_out, not_4_out, xor_1_out;

  and and_1 (and_1_out, not_1_out, not_2_out, not_3_out, input_4bit[0]);
  and and_2 (and_2_out, input_4bit[2], not_3_out, not_4_out);
  and and_3 (and_3_out, input_4bit[3], input_4bit[2]);
  or or_1 (A, and_1_out, and_2_out, and_3_out, and_4_out);
  and and_4 (and_4_out, input_4bit[3], input_4bit[1]);
  xor xor_1 (xor_1_out, input_4bit[1], input_4bit[0]);
  and and_5 (and_5_out, xor_1_out, input_4bit[2]);
  or or_2 (B, and_3_out, and_4_out, and_5_out);
  or or_3 (C, and_3_out, and_4_out, and_6_out);
  and and_6 (and_6_out, not_2_out, input_4bit[1], not_4_out);
  or or_4 (D, and_3_out, and_4_out, and_2_out, and_1_out, and_7_out);
  not not_1 (not_1_out, input_4bit[3]);
  not not_2 (not_2_out, input_4bit[2]);
  and and_7 (and_7_out, input_4bit[2], input_4bit[1], input_4bit[0]);
  not not_3 (not_3_out, input_4bit[1]);
  not not_4 (not_4_out, input_4bit[0]);
  and and_8 (and_8_out, input_4bit[2], not_3_out);
  or or_5 (E, and_4_out, and_8_out, input_4bit[0]);
  and and_9 (and_9_out, not_1_out, not_2_out, input_4bit[0]);
  and and_10 (and_10_out, not_2_out, input_4bit[1]);
  or or_6 (F, and_3_out, and_9_out, and_10_out, and_11_out);
  and and_11 (and_11_out, input_4bit[1], input_4bit[0]);
  and and_12 (and_12_out, input_4bit[3], input_4bit[1], input_4bit[0]);
  and and_13 (and_13_out, not_1_out, not_2_out, not_3_out);
  or or_7 (G, and_3_out, and_12_out, and_7_out, and_13_out);
endmodule

module seven_seg_selector (
  input  rst,
  input  clk,
  input  [3:0] Digit0,
  input  [3:0] Digit1,
  input  [3:0] Digit2,
  input  [3:0] Digit3,
  output [3:0] seven_seg_enable,
  output [3:0] selected_digit
);

  wire clock_divider_1_clk_out;
  wire [1:0] counter_1_q;

  clock_divider clock_divider_1 (.rst(rst), .clk_in(clk), .clk_out(clock_divider_1_clk_out));
  Counter #(.max('h3), .width(2)) counter_1 (
    .clr(rst), .count(1'b1), .clk(clock_divider_1_clk_out), .Q(counter_1_q));  // open: load, up, D, carry
  Multiplexer #(.select(2), .width(4)) multiplexer_1 (
    .in0(Digit0), .in1(Digit1), .in2(Digit2), .in3(Digit3), .out(selected_digit), .sel(counter_1_q));
  Decoder #(.enable("false"), .select(2)) decoder_1 (
    .out0(seven_seg_enable[0]), .out1(seven_seg_enable[1]), .out2(seven_seg_enable[2]),
    .out3(seven_seg_enable[3]), .sel(counter_1_q));
endmodule

module SSD_render (
  input  rst,
  input  CLK,
  input  [3:0] Digit0,
  input  [3:0] Digit1,
  input  [3:0] Digit2,
  input  [3:0] Digit3,
  output [3:0] seven_seg_enable,
  output A,
  output B,
  output C,
  output D,
  output E,
  output F,
  output G
);

  wire [3:0] seven_seg_selector_1_selected_digit;

  seven_seg_selector seven_seg_selector_1 (
    .rst(rst), .clk(CLK), .Digit0(Digit0), .Digit1(Digit1), .Digit2(Digit2), .Digit3(Digit3),
    .seven_seg_enable(seven_seg_enable), .selected_digit(seven_seg_selector_1_selected_digit));
  seven_seg_decoder seven_seg_decoder_1 (
    .input_4bit(seven_seg_selector_1_selected_digit), .A(A), .B(B), .C(C), .D(D), .E(E), .F(F), .G(G));
endmodule

module clock_divider (
  input  rst,
  input  clk_in,
  output clk_out
);

  Counter #(.max('h4), .width(32)) counter32bits (
    .clr(rst), .up(1'b1), .count(1'b1), .clk(clk_in), .carry(clk_out));  // open: load, D, Q
endmodule
