// Logisim project Sequential_Multiplier.circ as structural Verilog: 4 circuits, main circuit Sequential_8bit_Multiplier
module Sequential_8bit_Multiplier (
  input  rst,
  input  [7:0] InA,
  input  [7:0] InB,
  input  clk,
  input  BtnStart,
  output IsNeg,
  output [15:0] Outp,
  output IsDone
);

  wire multiplier_controlunit_1_sneg;
  wire [1:0] multiplier_controlunit_1_sa, multiplier_controlunit_1_sb, multiplier_controlunit_1_sc;

  Multiplier_ControlUnit multiplier_controlunit_1 (
    .rst(rst), .clk(clk), .BtnStart(BtnStart), .SA(multiplier_controlunit_1_sa),
    .SB(multiplier_controlunit_1_sb), .SC(multiplier_controlunit_1_sc), .IsDone(IsDone),
    .SNeg(multiplier_controlunit_1_sneg));
  Multiplier_DataPath multiplier_datapath_1 (
    .rst(rst), .InB(InB), .InA(InA), .clk(clk), .SA(multiplier_controlunit_1_sa),
    .SB(multiplier_controlunit_1_sb), .SC(multiplier_controlunit_1_sc), .SNeg(multiplier_controlunit_1_sneg),
    .IsNeg(IsNeg), .Outp(Outp));
endmodule

module Multiplier_DataPath (
  input  rst,
  input  [7:0] InB,
  input  [7:0] InA,
  input  clk,
  input  [1:0] SA,
  input  [1:0] SB,
  input  [1:0] SC,
  input  SNeg,
  output IsNeg,
  output [15:0] Outp
);

  wire multiplexer_1_out, xor_1_out;
  wire [7:0] multiplexer_2_out, multiplexer_3_out, negator_1_out, negator_2_out;
  wire [15:0] adder_1_out, allreg_16bit_1_outp, allreg_16bit_2_outp, multiplexer_4_out, multiplexer_5_out;

  D_Flip_Flop d_ff_1 (.D(multiplexer_1_out), .clk(clk), .Q(IsNeg), .reset(rst));  // open: Qn, preset
  Multiplexer multiplexer_1 (.in0(IsNeg), .in1(xor_1_out), .out(multiplexer_1_out), .sel(SNeg));
  xor xor_1 (xor_1_out, InB[7], InA[7]);
  Negator negator_1 (.in(InB), .out(negator_1_out));
  Negator negator_2 (.in(InA), .out(negator_2_out));
  Multiplexer #(.width(8)) multiplexer_2 (.in0(InB), .in1(negator_1_out), .out(multiplexer_2_out), .sel(InB[7]));
  Multiplexer #(.width(8)) multiplexer_3 (.in0(InA), .in1(negator_2_out), .out(multiplexer_3_out), .sel(InA[7]));
  AllReg_16bit allreg_16bit_1 (
    .Inp({{8{1'b0}}, multiplexer_2_out}), .Sig(SB), .clk(clk), .rst(rst), .Outp(allreg_16bit_1_outp));
  AllReg_16bit allreg_16bit_2 (
    .Inp({{8{1'b0}}, multiplexer_3_out}), .Sig(SA), .clk(clk), .rst(rst), .Outp(allreg_16bit_2_outp));
  Multiplexer #(.width(16)) multiplexer_4 (
    .in0({16{1'b0}}), .in1(allreg_16bit_2_outp), .out(multiplexer_4_out), .sel(allreg_16bit_1_outp[0]));
  Adder #(.width(16)) adder_1 (.a(multiplexer_4_out), .b(Outp), .out(adder_1_out));  // open: cin, cout
  Multiplexer #(.select(2), .width(16)) multiplexer_5 (
    .in0(Outp), .in1(adder_1_out), .in2({16{1'b0}}), .in3({16{1'b0}}), .out(multiplexer_5_out), .sel(SC));
  AllReg_16bit allreg_16bit_3 (.Inp(multiplexer_5_out), .Sig(2'b00), .clk(clk), .rst(rst), .Outp(Outp));

  // Notes on the sheet:
  //   Abs B
  //   Abs A
endmodule

module AllReg_16bit (
  input  [15:0] Inp,
  input  [1:0] Sig,
  input  clk,
  input  rst,
  output [15:0] Outp
);

  wire multiplexer_1_out, multiplexer_2_out, multiplexer_3_out, multiplexer_4_out, multiplexer_5_out,
       multiplexer_6_out, multiplexer_7_out, multiplexer_8_out, multiplexer_9_out, multiplexer_10_out,
       multiplexer_11_out, multiplexer_12_out, multiplexer_13_out, multiplexer_14_out, multiplexer_15_out,
       multiplexer_16_out;

  Multiplexer #(.select(2)) multiplexer_1 (
    .in0(Inp[15]), .in1(1'b0), .in2(Outp[14]), .in3(Outp[15]), .out(multiplexer_1_out), .sel(Sig));
  D_Flip_Flop d_ff_1 (.D(multiplexer_1_out), .clk(clk), .Q(Outp[15]), .reset(rst));  // open: Qn, preset
  Multiplexer #(.select(2)) multiplexer_2 (
    .in0(Inp[14]), .in1(Outp[15]), .in2(Outp[13]), .in3(Outp[14]), .out(multiplexer_2_out), .sel(Sig));
  D_Flip_Flop d_ff_2 (.D(multiplexer_2_out), .clk(clk), .Q(Outp[14]), .reset(rst));  // open: Qn, preset
  Multiplexer #(.select(2)) multiplexer_3 (
    .in0(Inp[13]), .in1(Outp[14]), .in2(Outp[12]), .in3(Outp[13]), .out(multiplexer_3_out), .sel(Sig));
  D_Flip_Flop d_ff_3 (.D(multiplexer_3_out), .clk(clk), .Q(Outp[13]), .reset(rst));  // open: Qn, preset
  Multiplexer #(.select(2)) multiplexer_4 (
    .in0(Inp[12]), .in1(Outp[13]), .in2(Outp[11]), .in3(Outp[12]), .out(multiplexer_4_out), .sel(Sig));
  D_Flip_Flop d_ff_4 (.D(multiplexer_4_out), .clk(clk), .Q(Outp[12]), .reset(rst));  // open: Qn, preset
  Multiplexer #(.select(2)) multiplexer_5 (
    .in0(Inp[11]), .in1(Outp[12]), .in2(Outp[10]), .in3(Outp[11]), .out(multiplexer_5_out), .sel(Sig));
  D_Flip_Flop d_ff_5 (.D(multiplexer_5_out), .clk(clk), .Q(Outp[11]), .reset(rst));  // open: Qn, preset
  Multiplexer #(.select(2)) multiplexer_6 (
    .in0(Inp[10]), .in1(Outp[11]), .in2(Outp[9]), .in3(Outp[10]), .out(multiplexer_6_out), .sel(Sig));
  D_Flip_Flop d_ff_6 (.D(multiplexer_6_out), .clk(clk), .Q(Outp[10]), .reset(rst));  // open: Qn, preset
  Multiplexer #(.select(2)) multiplexer_7 (
    .in0(Inp[9]), .in1(Outp[10]), .in2(Outp[8]), .in3(Outp[9]), .out(multiplexer_7_out), .sel(Sig));
  D_Flip_Flop d_ff_7 (.D(multiplexer_7_out), .clk(clk), .Q(Outp[9]), .reset(rst));  // open: Qn, preset
  Multiplexer #(.select(2)) multiplexer_8 (
    .in0(Inp[8]), .in1(Outp[9]), .in2(Outp[7]), .in3(Outp[8]), .out(multiplexer_8_out), .sel(Sig));
  D_Flip_Flop d_ff_8 (.D(multiplexer_8_out), .clk(clk), .Q(Outp[8]), .reset(rst));  // open: Qn, preset
  Multiplexer #(.select(2)) multiplexer_9 (
    .in0(Inp[7]), .in1(Outp[8]), .in2(Outp[6]), .in3(Outp[7]), .out(multiplexer_9_out), .sel(Sig));
  D_Flip_Flop d_ff_9 (.D(multiplexer_9_out), .clk(clk), .Q(Outp[7]), .reset(rst));  // open: Qn, preset
  Multiplexer #(.select(2)) multiplexer_10 (
    .in0(Inp[6]), .in1(Outp[7]), .in2(Outp[5]), .in3(Outp[6]), .out(multiplexer_10_out), .sel(Sig));
  D_Flip_Flop d_ff_10 (.D(multiplexer_10_out), .clk(clk), .Q(Outp[6]), .reset(rst));  // open: Qn, preset
  Multiplexer #(.select(2)) multiplexer_11 (
    .in0(Inp[5]), .in1(Outp[6]), .in2(Outp[4]), .in3(Outp[5]), .out(multiplexer_11_out), .sel(Sig));
  D_Flip_Flop d_ff_11 (.D(multiplexer_11_out), .clk(clk), .Q(Outp[5]), .reset(rst));  // open: Qn, preset
  Multiplexer #(.select(2)) multiplexer_12 (
    .in0(Inp[4]), .in1(Outp[5]), .in2(Outp[3]), .in3(Outp[4]), .out(multiplexer_12_out), .sel(Sig));
  D_Flip_Flop d_ff_12 (.D(multiplexer_12_out), .clk(clk), .Q(Outp[4]), .reset(rst));  // open: Qn, preset
  Multiplexer #(.select(2)) multiplexer_13 (
    .in0(Inp[3]), .in1(Outp[4]), .in2(Outp[2]), .in3(Outp[3]), .out(multiplexer_13_out), .sel(Sig));
  D_Flip_Flop d_ff_13 (.D(multiplexer_13_out), .clk(clk), .Q(Outp[3]), .reset(rst));  // open: Qn, preset
  Multiplexer #(.select(2)) multiplexer_14 (
    .in0(Inp[2]), .in1(Outp[3]), .in2(Outp[1]), .in3(Outp[2]), .out(multiplexer_14_out), .sel(Sig));
  D_Flip_Flop d_ff_14 (.D(multiplexer_14_out), .clk(clk), .Q(Outp[2]), .reset(rst));  // open: Qn, preset
  Multiplexer #(.select(2)) multiplexer_15 (
    .in0(Inp[1]), .in1(Outp[2]), .in2(Outp[0]), .in3(Outp[1]), .out(multiplexer_15_out), .sel(Sig));
  D_Flip_Flop d_ff_15 (.D(multiplexer_15_out), .clk(clk), .Q(Outp[1]), .reset(rst));  // open: Qn, preset
  Multiplexer #(.select(2)) multiplexer_16 (
    .in0(Inp[0]), .in1(Outp[1]), .in2(1'b0), .in3(Outp[0]), .out(multiplexer_16_out), .sel(Sig));
  D_Flip_Flop d_ff_16 (.D(multiplexer_16_out), .clk(clk), .Q(Outp[0]), .reset(rst));  // open: Qn, preset
endmodule

module Multiplier_ControlUnit (
  input  rst,
  input  clk,
  input  BtnStart,
  output [1:0] SA,
  output [1:0] SB,
  output [1:0] SC,
  output IsDone,
  output SNeg
);

  wire and_3_out, and_4_out, counter_1_carry, Is8_out, Is9_out, nor_1_out, not_1_out, not_2_out, not_3_out,
       not_4_out, not_5_out, not_6_out, not_7_out, not_8_out, not_9_out, not_10_out, not_11_out, not_12_out,
       not_13_out;
  wire [1:0] and_1_out;
  wire [3:0] counter_1_q;

  Counter #(.max('hb), .width(4)) counter_1 (
    .load(rst), .up(1'b1), .count(nor_1_out), .clk(clk), .D(4'b1001), .carry(counter_1_carry), .Q(counter_1_q));  // open: clr
  Multiplexer #(.select(2), .width(2)) multiplexer_1 (
    .in0(2'b11), .in1(2'b00), .in2(2'b10), .in3(2'b10), .out(SA), .sel(and_1_out));
  Multiplexer #(.select(2), .width(2)) multiplexer_2 (
    .in0(2'b11), .in1(2'b00), .in2(2'b01), .in3(2'b01), .out(SB), .sel(and_1_out));
  not not_1 (not_1_out, Is8_out);
  and and_1 (and_1_out[0], not_1_out, not_2_out, SNeg);
  not not_2 (not_2_out, Is9_out);
  not not_3 (not_3_out, Is8_out);
  and and_2 (and_1_out[1], not_3_out, not_4_out, not_5_out);
  not not_4 (not_4_out, Is9_out);
  not not_5 (not_5_out, SNeg);
  not not_6 (not_6_out, counter_1_q[0]);
  not not_7 (not_7_out, counter_1_q[1]);
  not not_8 (not_8_out, counter_1_q[2]);
  not not_9 (not_9_out, counter_1_q[1]);
  not not_10 (not_10_out, counter_1_q[2]);
  not not_11 (not_11_out, counter_1_q[0]);
  not not_12 (not_12_out, counter_1_q[2]);
  Multiplexer #(.select(2), .width(2)) multiplexer_3 (
    .in0(2'b00), .in1(2'b10), .in2(2'b01), .in3(2'b01), .out(SC), .sel(and_1_out));
  and Is8 (Is8_out, not_6_out, not_7_out, not_8_out, counter_1_q[3]);
  and Is9 (Is9_out, counter_1_q[0], not_9_out, not_10_out, counter_1_q[3]);
  and Is10 (SNeg, not_11_out, counter_1_q[1], not_12_out, counter_1_q[3]);
  nor nor_1 (nor_1_out, and_3_out, and_4_out);
  and and_3 (and_3_out, Is8_out, BtnStart);
  or or_1 (IsDone, Is8_out, Is9_out);
  and and_4 (and_4_out, not_13_out, Is9_out);
  not not_13 (not_13_out, BtnStart);

  // Notes on the sheet:
  //   Load / store
  //   SHR / acc
  //   SHL / rst
  //   Store / rst
endmodule
