// Logisim project Signed_8bit_multiplier.circ as structural Verilog: 1 circuit, main circuit main
module main (
  input  BTN_R,
  input  BTN_L,
  input  Start,
  input  rst,
  input  [7:0] in_5,
  input  [7:0] in_6,
  output Is_Done,
  output A,
  output B,
  output C,
  output D,
  output E,
  output F,
  output G
);

  wire and_1_out, clock_1_out, push_button_1_outputpushbutton, push_button_2_outputpushbutton,
       push_button_3_outputpushbutton, sequential_8bit_multiplier_1_isdone,
       sequential_8bit_multiplier_1_isneg;
  wire [3:0] digit_shifter_1_digit_out_0, digit_shifter_1_digit_out_1, digit_shifter_1_digit_out_2,
       digit_shifter_1_digit_out_3, slicerdoubledabble_1_digit0, slicerdoubledabble_1_digit1,
       slicerdoubledabble_1_digit2, slicerdoubledabble_1_digit3, slicerdoubledabble_1_digit4,
       ssd_render_1_seven_seg_enable;
  wire [6:0] multiplexer_1_out, multiplexer_2_out, multiplexer_3_out, multiplexer_4_out;
  wire [15:0] sequential_8bit_multiplier_1_outp;

  Clock clock_1 (.out(clock_1_out));
  _7_Segment_Display #(.active("false"), .decimalPoint("false")) u_7_segment_display_1 (
    .g(multiplexer_1_out[6]), .f(multiplexer_1_out[5]), .a(multiplexer_1_out[0]), .b(multiplexer_1_out[1]),
    .e(multiplexer_1_out[4]), .d(multiplexer_1_out[3]), .c(multiplexer_1_out[2]));
  Multiplexer #(.width(7)) multiplexer_1 (
    .in0({7{1'b1}}), .in1({G, F, E, D, C, B, A}), .out(multiplexer_1_out),
    .sel(ssd_render_1_seven_seg_enable[3]));
  Push_Button push_button_1 (
    .InputPushButton(BTN_R), .clk(clock_1_out), .rst(rst), .OutputPushButton(push_button_1_outputpushbutton));
  Push_Button push_button_2 (
    .InputPushButton(BTN_L), .clk(clock_1_out), .rst(rst), .OutputPushButton(push_button_2_outputpushbutton));
  Push_Button push_button_3 (
    .InputPushButton(Start), .clk(clock_1_out), .rst(rst), .OutputPushButton(push_button_3_outputpushbutton));
  and and_1 (and_1_out, Is_Done, push_button_3_outputpushbutton);
  _7_Segment_Display #(.active("false"), .decimalPoint("false")) u_7_segment_display_2 (
    .g(multiplexer_2_out[6]), .f(multiplexer_2_out[5]), .a(multiplexer_2_out[0]), .b(multiplexer_2_out[1]),
    .e(multiplexer_2_out[4]), .d(multiplexer_2_out[3]), .c(multiplexer_2_out[2]));
  Multiplexer #(.width(7)) multiplexer_2 (
    .in0({7{1'b1}}), .in1({G, F, E, D, C, B, A}), .out(multiplexer_2_out),
    .sel(ssd_render_1_seven_seg_enable[2]));
  _7_Segment_Display #(.active("false"), .decimalPoint("false")) u_7_segment_display_3 (
    .g(multiplexer_3_out[6]), .f(multiplexer_3_out[5]), .a(multiplexer_3_out[0]), .b(multiplexer_3_out[1]),
    .e(multiplexer_3_out[4]), .d(multiplexer_3_out[3]), .c(multiplexer_3_out[2]));
  Multiplexer #(.width(7)) multiplexer_3 (
    .in0({7{1'b1}}), .in1({G, F, E, D, C, B, A}), .out(multiplexer_3_out),
    .sel(ssd_render_1_seven_seg_enable[1]));
  Sequential_8bit_Multiplier sequential_8bit_multiplier_1 (
    .rst(rst), .InA(in_5), .InB(in_6), .clk(clock_1_out), .BtnStart(and_1_out),
    .IsNeg(sequential_8bit_multiplier_1_isneg), .Outp(sequential_8bit_multiplier_1_outp),
    .IsDone(sequential_8bit_multiplier_1_isdone));
  _7_Segment_Display #(.active("false"), .decimalPoint("false")) u_7_segment_display_4 (
    .g(multiplexer_4_out[6]), .f(multiplexer_4_out[5]), .a(multiplexer_4_out[0]), .b(multiplexer_4_out[1]),
    .e(multiplexer_4_out[4]), .d(multiplexer_4_out[3]), .c(multiplexer_4_out[2]));
  Multiplexer #(.width(7)) multiplexer_4 (
    .in0({7{1'b1}}), .in1({G, F, E, D, C, B, A}), .out(multiplexer_4_out),
    .sel(ssd_render_1_seven_seg_enable[0]));
  slicerDoubleDabble slicerdoubledabble_1 (
    .rst(rst), .clk(clock_1_out), .start(sequential_8bit_multiplier_1_isdone),
    .num(sequential_8bit_multiplier_1_outp), .isDone(Is_Done), .Digit0(slicerdoubledabble_1_digit0),
    .Digit1(slicerdoubledabble_1_digit1), .Digit2(slicerdoubledabble_1_digit2),
    .Digit3(slicerdoubledabble_1_digit3), .Digit4(slicerdoubledabble_1_digit4));
  digit_shifter digit_shifter_1 (
    .rst(rst), .BTN_R(push_button_1_outputpushbutton), .BTN_L(push_button_2_outputpushbutton),
    .Start(and_1_out), .CLK(clock_1_out), .Digit_0(slicerdoubledabble_1_digit0),
    .Digit_1(slicerdoubledabble_1_digit1), .Digit_2(slicerdoubledabble_1_digit2),
    .Digit_3(slicerdoubledabble_1_digit3), .Digit_4(slicerdoubledabble_1_digit4),
    .IsNeg(sequential_8bit_multiplier_1_isneg), .Digit_out_0(digit_shifter_1_digit_out_0),
    .Digit_out_1(digit_shifter_1_digit_out_1), .Digit_out_2(digit_shifter_1_digit_out_2),
    .Digit_out_3(digit_shifter_1_digit_out_3));
  SSD_render ssd_render_1 (
    .rst(rst), .CLK(clock_1_out), .Digit0(digit_shifter_1_digit_out_0), .Digit1(digit_shifter_1_digit_out_1),
    .Digit2(digit_shifter_1_digit_out_2), .Digit3(digit_shifter_1_digit_out_3),
    .seven_seg_enable(ssd_render_1_seven_seg_enable), .A(A), .B(B), .C(C), .D(D), .E(E), .F(F), .G(G));
endmodule
