// Logisim project digit_shifter_circuit.circ as structural Verilog: 3 circuits, main circuit digit_shifter
module digit_shifter (
  input  rst,
  input  BTN_R,
  input  BTN_L,
  input  Start,
  input  CLK,
  input  [3:0] Digit_0,
  input  [3:0] Digit_1,
  input  [3:0] Digit_2,
  input  [3:0] Digit_3,
  input  [3:0] Digit_4,
  input  IsNeg,
  output [3:0] Digit_out_0,
  output [3:0] Digit_out_1,
  output [3:0] Digit_out_2,
  output [3:0] Digit_out_3
);

  wire [1:0] control_unit_digit_shifter_1_out_6;

  control_unit_digit_shifter control_unit_digit_shifter_1 (
    .rst(rst), .BTN_R(BTN_R), .BTN_L(BTN_L), .Start(Start), .CLK(CLK),
    .out_6(control_unit_digit_shifter_1_out_6));
  DataPath_DigitShifter datapath_digitshifter_1 (
    .DigitSelector(control_unit_digit_shifter_1_out_6), .Digit_0(Digit_0), .Digit_1(Digit_1),
    .Digit_2(Digit_2), .Digit_3(Digit_3), .Digit_4(Digit_4), .is_Neg(IsNeg), .Digit_out_0(Digit_out_0),
    .Digit_out_1(Digit_out_1), .Digit_out_2(Digit_out_2), .Digit_out_3(Digit_out_3));
endmodule

module control_unit_digit_shifter (
  input  rst,
  input  BTN_R,
  input  BTN_L,
  input  Start,
  input  CLK,
  output [1:0] out_6
);

  wire and_1_out, and_2_out, nand_1_out, nand_2_out, not_1_out, not_2_out, or_1_out, or_2_out;

  not not_1 (not_1_out, out_6[1]);
  not not_2 (not_2_out, out_6[0]);
  nand nand_1 (nand_1_out, not_1_out, not_2_out);
  and and_1 (and_1_out, nand_1_out, BTN_L);
  or or_1 (or_1_out, and_1_out, and_2_out);
  nand nand_2 (nand_2_out, out_6[1], not_2_out);
  and and_2 (and_2_out, BTN_R, nand_2_out);
  or or_2 (or_2_out, Start, rst);
  Counter #(.max('h3), .width(2)) counter_1 (
    .load(or_2_out), .up(BTN_R), .count(or_1_out), .clk(CLK), .D(2'b10), .Q(out_6));  // open: clr, carry
endmodule

module DataPath_DigitShifter (
  input  [1:0] DigitSelector,
  input  [3:0] Digit_0,
  input  [3:0] Digit_1,
  input  [3:0] Digit_2,
  input  [3:0] Digit_3,
  input  [3:0] Digit_4,
  input  is_Neg,
  output [3:0] Digit_out_0,
  output [3:0] Digit_out_1,
  output [3:0] Digit_out_2,
  output [3:0] Digit_out_3
);

  Multiplexer #(.width(4)) multiplexer_1 (.in0(4'b1111), .in1(4'b1010), .out(Digit_out_3), .sel(is_Neg));
  Multiplexer #(.select(2), .width(4)) multiplexer_2 (
    .in0(Digit_2), .in1(Digit_1), .in2(Digit_0), .in3(Digit_0), .out(Digit_out_0), .sel(DigitSelector));
  Multiplexer #(.select(2), .width(4)) multiplexer_3 (
    .in0(Digit_3), .in1(Digit_2), .in2(Digit_1), .in3(Digit_1), .out(Digit_out_1), .sel(DigitSelector));
  Multiplexer #(.select(2), .width(4)) multiplexer_4 (
    .in0(Digit_4), .in1(Digit_3), .in2(Digit_2), .in3(Digit_2), .out(Digit_out_2), .sel(DigitSelector));
endmodule
