// Logisim project mod10_slicer.circ as structural Verilog: 2 circuits, main circuit Mod10_adder
module Mod10_adder (
  input  Cin,
  input  [3:0] A,
  input  [3:0] B,
  output Cout,
  output [3:0] mod10_out
);

  wire adder_1_cout, and_1_out, not_1_out, or_2_out;
  wire [3:0] adder_1_out;
  wire [3:1] not_2_out;

  or or_1 (Cout, adder_1_cout, and_1_out);
  and and_1 (and_1_out, adder_1_out[3], or_2_out);
  xor xor_1 (not_2_out[3], adder_1_out[3], or_2_out);
  Multiplexer #(.width(4)) multiplexer_1 (
    .in0(adder_1_out), .in1({not_2_out, adder_1_out[0]}), .out(mod10_out), .sel(Cout));
  Adder #(.width(4)) adder_1 (.a(A), .b(B), .out(adder_1_out), .cin(Cin), .cout(adder_1_cout));
  or or_2 (or_2_out, adder_1_out[2], adder_1_out[1]);
  xor xor_2 (not_2_out[2], not_1_out, adder_1_out[1]);
  not not_1 (not_1_out, adder_1_out[2]);
  not not_2 (not_2_out[1], adder_1_out[1]);
endmodule

module BCD (
  input  [15:0] product_16bit,
  output [3:0] digit_1,
  output [3:0] digit_2,
  output [3:0] digit_3,
  output [3:0] digit_4,
  output [3:0] digit_5
);

  wire mod10_adder_1_cout, mod10_adder_2_cout, mod10_adder_3_cout, mod10_adder_4_cout, mod10_adder_6_cout,
       mod10_adder_7_cout, mod10_adder_8_cout, mod10_adder_9_cout, mod10_adder_11_cout, mod10_adder_12_cout,
       mod10_adder_13_cout, mod10_adder_14_cout, mod10_adder_16_cout, mod10_adder_17_cout,
       mod10_adder_18_cout, mod10_adder_19_cout, mod10_adder_21_cout, mod10_adder_22_cout,
       mod10_adder_23_cout, mod10_adder_24_cout, mod10_adder_26_cout, mod10_adder_27_cout,
       mod10_adder_28_cout, mod10_adder_29_cout, mod10_adder_31_cout, mod10_adder_32_cout,
       mod10_adder_33_cout, mod10_adder_34_cout, mod10_adder_36_cout, mod10_adder_37_cout,
       mod10_adder_38_cout, mod10_adder_39_cout, mod10_adder_41_cout, mod10_adder_42_cout,
       mod10_adder_43_cout, mod10_adder_44_cout, mod10_adder_46_cout, mod10_adder_47_cout,
       mod10_adder_48_cout, mod10_adder_49_cout, mod10_adder_51_cout, mod10_adder_52_cout,
       mod10_adder_53_cout, mod10_adder_54_cout, mod10_adder_56_cout, mod10_adder_57_cout,
       mod10_adder_58_cout, mod10_adder_59_cout, mod10_adder_61_cout, mod10_adder_62_cout,
       mod10_adder_63_cout, mod10_adder_64_cout, mod10_adder_66_cout, mod10_adder_67_cout,
       mod10_adder_68_cout, mod10_adder_69_cout, mod10_adder_71_cout, mod10_adder_72_cout,
       mod10_adder_73_cout, mod10_adder_74_cout;
  wire [3:0] mod10_adder_1_mod10_out, mod10_adder_2_mod10_out, mod10_adder_3_mod10_out,
       mod10_adder_4_mod10_out, mod10_adder_5_mod10_out, mod10_adder_6_mod10_out, mod10_adder_7_mod10_out,
       mod10_adder_8_mod10_out, mod10_adder_9_mod10_out, mod10_adder_10_mod10_out, mod10_adder_11_mod10_out,
       mod10_adder_12_mod10_out, mod10_adder_13_mod10_out, mod10_adder_14_mod10_out,
       mod10_adder_15_mod10_out, mod10_adder_16_mod10_out, mod10_adder_17_mod10_out,
       mod10_adder_18_mod10_out, mod10_adder_19_mod10_out, mod10_adder_20_mod10_out,
       mod10_adder_21_mod10_out, mod10_adder_22_mod10_out, mod10_adder_23_mod10_out,
       mod10_adder_24_mod10_out, mod10_adder_25_mod10_out, mod10_adder_26_mod10_out,
       mod10_adder_27_mod10_out, mod10_adder_28_mod10_out, mod10_adder_29_mod10_out,
       mod10_adder_30_mod10_out, mod10_adder_31_mod10_out, mod10_adder_32_mod10_out,
       mod10_adder_33_mod10_out, mod10_adder_34_mod10_out, mod10_adder_35_mod10_out,
       mod10_adder_36_mod10_out, mod10_adder_37_mod10_out, mod10_adder_38_mod10_out,
       mod10_adder_39_mod10_out, mod10_adder_40_mod10_out, mod10_adder_41_mod10_out,
       mod10_adder_42_mod10_out, mod10_adder_43_mod10_out, mod10_adder_44_mod10_out,
       mod10_adder_45_mod10_out, mod10_adder_46_mod10_out, mod10_adder_47_mod10_out,
       mod10_adder_48_mod10_out, mod10_adder_49_mod10_out, mod10_adder_50_mod10_out,
       mod10_adder_51_mod10_out, mod10_adder_52_mod10_out, mod10_adder_53_mod10_out,
       mod10_adder_54_mod10_out, mod10_adder_55_mod10_out, mod10_adder_56_mod10_out,
       mod10_adder_57_mod10_out, mod10_adder_58_mod10_out, mod10_adder_59_mod10_out,
       mod10_adder_60_mod10_out, mod10_adder_61_mod10_out, mod10_adder_62_mod10_out,
       mod10_adder_63_mod10_out, mod10_adder_64_mod10_out, mod10_adder_65_mod10_out,
       mod10_adder_66_mod10_out, mod10_adder_67_mod10_out, mod10_adder_68_mod10_out,
       mod10_adder_69_mod10_out, mod10_adder_70_mod10_out, multiplexer_1_out, multiplexer_2_out,
       multiplexer_3_out, multiplexer_4_out, multiplexer_5_out, multiplexer_6_out, multiplexer_7_out,
       multiplexer_8_out, multiplexer_9_out, multiplexer_10_out, multiplexer_11_out, multiplexer_12_out,
       multiplexer_13_out, multiplexer_14_out, multiplexer_15_out, multiplexer_16_out, multiplexer_17_out,
       multiplexer_18_out, multiplexer_19_out, multiplexer_20_out, multiplexer_21_out, multiplexer_22_out,
       multiplexer_23_out, multiplexer_24_out, multiplexer_25_out, multiplexer_26_out, multiplexer_27_out,
       multiplexer_28_out, multiplexer_29_out, multiplexer_30_out, multiplexer_31_out, multiplexer_32_out,
       multiplexer_33_out, multiplexer_34_out, multiplexer_35_out, multiplexer_36_out, multiplexer_37_out,
       multiplexer_38_out, multiplexer_39_out, multiplexer_40_out, multiplexer_41_out, multiplexer_42_out,
       multiplexer_43_out, multiplexer_44_out, multiplexer_45_out, multiplexer_46_out, multiplexer_47_out,
       multiplexer_48_out, multiplexer_49_out, multiplexer_50_out, multiplexer_51_out, multiplexer_52_out,
       multiplexer_53_out, multiplexer_54_out, multiplexer_55_out, multiplexer_56_out, multiplexer_57_out,
       multiplexer_58_out, multiplexer_59_out, multiplexer_60_out, multiplexer_61_out, multiplexer_62_out,
       multiplexer_63_out, multiplexer_64_out, multiplexer_65_out, multiplexer_66_out, multiplexer_67_out,
       multiplexer_68_out, multiplexer_69_out, multiplexer_70_out, multiplexer_71_out, multiplexer_72_out,
       multiplexer_73_out, multiplexer_74_out, multiplexer_75_out, multiplexer_76_out, multiplexer_77_out,
       multiplexer_78_out, multiplexer_79_out, multiplexer_80_out;

  Multiplexer #(.width(4)) multiplexer_1 (
    .in0(4'b0000), .in1(4'b0001), .out(multiplexer_1_out), .sel(product_16bit[0]));
  Multiplexer #(.width(4)) multiplexer_2 (
    .in0(4'b0000), .in1(4'b0010), .out(multiplexer_2_out), .sel(product_16bit[1]));
  Multiplexer #(.width(4)) multiplexer_3 (
    .in0(4'b0000), .in1(4'b0000), .out(multiplexer_3_out), .sel(product_16bit[0]));
  Multiplexer #(.width(4)) multiplexer_4 (
    .in0(4'b0000), .in1(4'b0000), .out(multiplexer_4_out), .sel(product_16bit[1]));
  Multiplexer #(.width(4)) multiplexer_5 (
    .in0(4'b0000), .in1(4'b0000), .out(multiplexer_5_out), .sel(product_16bit[0]));
  Multiplexer #(.width(4)) multiplexer_6 (
    .in0(4'b0000), .in1(4'b0000), .out(multiplexer_6_out), .sel(product_16bit[1]));
  Multiplexer #(.width(4)) multiplexer_7 (
    .in0(4'b0000), .in1(4'b0000), .out(multiplexer_7_out), .sel(product_16bit[0]));
  Multiplexer #(.width(4)) multiplexer_8 (
    .in0(4'b0000), .in1(4'b0000), .out(multiplexer_8_out), .sel(product_16bit[1]));
  Multiplexer #(.width(4)) multiplexer_9 (
    .in0(4'b0000), .in1(4'b0000), .out(multiplexer_9_out), .sel(product_16bit[0]));
  Multiplexer #(.width(4)) multiplexer_10 (
    .in0(4'b0000), .in1(4'b0000), .out(multiplexer_10_out), .sel(product_16bit[1]));
  Multiplexer #(.width(4)) multiplexer_11 (
    .in0(4'b0000), .in1(4'b0100), .out(multiplexer_11_out), .sel(product_16bit[2]));
  Mod10_adder mod10_adder_1 (
    .Cin(1'b0), .A(multiplexer_1_out), .B(multiplexer_2_out), .Cout(mod10_adder_1_cout),
    .mod10_out(mod10_adder_1_mod10_out));
  Multiplexer #(.width(4)) multiplexer_12 (
    .in0(4'b0000), .in1(4'b0000), .out(multiplexer_12_out), .sel(product_16bit[2]));
  Mod10_adder mod10_adder_2 (
    .Cin(mod10_adder_1_cout), .A(multiplexer_3_out), .B(multiplexer_4_out), .Cout(mod10_adder_2_cout),
    .mod10_out(mod10_adder_2_mod10_out));
  Multiplexer #(.width(4)) multiplexer_13 (
    .in0(4'b0000), .in1(4'b0000), .out(multiplexer_13_out), .sel(product_16bit[2]));
  Mod10_adder mod10_adder_3 (
    .Cin(mod10_adder_2_cout), .A(multiplexer_5_out), .B(multiplexer_6_out), .Cout(mod10_adder_3_cout),
    .mod10_out(mod10_adder_3_mod10_out));
  Multiplexer #(.width(4)) multiplexer_14 (
    .in0(4'b0000), .in1(4'b0000), .out(multiplexer_14_out), .sel(product_16bit[2]));
  Mod10_adder mod10_adder_4 (
    .Cin(mod10_adder_3_cout), .A(multiplexer_7_out), .B(multiplexer_8_out), .Cout(mod10_adder_4_cout),
    .mod10_out(mod10_adder_4_mod10_out));
  Multiplexer #(.width(4)) multiplexer_15 (
    .in0(4'b0000), .in1(4'b0000), .out(multiplexer_15_out), .sel(product_16bit[2]));
  Mod10_adder mod10_adder_5 (
    .Cin(mod10_adder_4_cout), .A(multiplexer_9_out), .B(multiplexer_10_out),
    .mod10_out(mod10_adder_5_mod10_out));  // open: Cout
  Mod10_adder mod10_adder_6 (
    .Cin(1'b0), .A(multiplexer_11_out), .B(mod10_adder_1_mod10_out), .Cout(mod10_adder_6_cout),
    .mod10_out(mod10_adder_6_mod10_out));
  Mod10_adder mod10_adder_7 (
    .Cin(mod10_adder_6_cout), .A(multiplexer_12_out), .B(mod10_adder_2_mod10_out), .Cout(mod10_adder_7_cout),
    .mod10_out(mod10_adder_7_mod10_out));
  Mod10_adder mod10_adder_8 (
    .Cin(mod10_adder_7_cout), .A(multiplexer_13_out), .B(mod10_adder_3_mod10_out), .Cout(mod10_adder_8_cout),
    .mod10_out(mod10_adder_8_mod10_out));
  Mod10_adder mod10_adder_9 (
    .Cin(mod10_adder_8_cout), .A(multiplexer_14_out), .B(mod10_adder_4_mod10_out), .Cout(mod10_adder_9_cout),
    .mod10_out(mod10_adder_9_mod10_out));
  Mod10_adder mod10_adder_10 (
    .Cin(mod10_adder_9_cout), .A(multiplexer_15_out), .B(mod10_adder_5_mod10_out),
    .mod10_out(mod10_adder_10_mod10_out));  // open: Cout
  Multiplexer #(.width(4)) multiplexer_16 (
    .in0(4'b0000), .in1(4'b1000), .out(multiplexer_16_out), .sel(product_16bit[3]));
  Multiplexer #(.width(4)) multiplexer_17 (
    .in0(4'b0000), .in1(4'b0000), .out(multiplexer_17_out), .sel(product_16bit[3]));
  Multiplexer #(.width(4)) multiplexer_18 (
    .in0(4'b0000), .in1(4'b0000), .out(multiplexer_18_out), .sel(product_16bit[3]));
  Multiplexer #(.width(4)) multiplexer_19 (
    .in0(4'b0000), .in1(4'b0000), .out(multiplexer_19_out), .sel(product_16bit[3]));
  Multiplexer #(.width(4)) multiplexer_20 (
    .in0(4'b0000), .in1(4'b0000), .out(multiplexer_20_out), .sel(product_16bit[3]));
  Multiplexer #(.width(4)) multiplexer_21 (
    .in0(4'b0000), .in1(4'b0110), .out(multiplexer_21_out), .sel(product_16bit[4]));
  Mod10_adder mod10_adder_11 (
    .Cin(1'b0), .A(multiplexer_16_out), .B(mod10_adder_6_mod10_out), .Cout(mod10_adder_11_cout),
    .mod10_out(mod10_adder_11_mod10_out));
  Multiplexer #(.width(4)) multiplexer_22 (
    .in0(4'b0000), .in1(4'b0001), .out(multiplexer_22_out), .sel(product_16bit[4]));
  Mod10_adder mod10_adder_12 (
    .Cin(mod10_adder_11_cout), .A(multiplexer_17_out), .B(mod10_adder_7_mod10_out),
    .Cout(mod10_adder_12_cout), .mod10_out(mod10_adder_12_mod10_out));
  Multiplexer #(.width(4)) multiplexer_23 (
    .in0(4'b0000), .in1(4'b0000), .out(multiplexer_23_out), .sel(product_16bit[4]));
  Mod10_adder mod10_adder_13 (
    .Cin(mod10_adder_12_cout), .A(multiplexer_18_out), .B(mod10_adder_8_mod10_out),
    .Cout(mod10_adder_13_cout), .mod10_out(mod10_adder_13_mod10_out));
  Multiplexer #(.width(4)) multiplexer_24 (
    .in0(4'b0000), .in1(4'b0000), .out(multiplexer_24_out), .sel(product_16bit[4]));
  Mod10_adder mod10_adder_14 (
    .Cin(mod10_adder_13_cout), .A(multiplexer_19_out), .B(mod10_adder_9_mod10_out),
    .Cout(mod10_adder_14_cout), .mod10_out(mod10_adder_14_mod10_out));
  Multiplexer #(.width(4)) multiplexer_25 (
    .in0(4'b0000), .in1(4'b0000), .out(multiplexer_25_out), .sel(product_16bit[4]));
  Mod10_adder mod10_adder_15 (
    .Cin(mod10_adder_14_cout), .A(multiplexer_20_out), .B(mod10_adder_10_mod10_out),
    .mod10_out(mod10_adder_15_mod10_out));  // open: Cout
  Multiplexer #(.width(4)) multiplexer_26 (
    .in0(4'b0000), .in1(4'b0010), .out(multiplexer_26_out), .sel(product_16bit[5]));
  Mod10_adder mod10_adder_16 (
    .Cin(1'b0), .A(multiplexer_21_out), .B(mod10_adder_11_mod10_out), .Cout(mod10_adder_16_cout),
    .mod10_out(mod10_adder_16_mod10_out));
  Multiplexer #(.width(4)) multiplexer_27 (
    .in0(4'b0000), .in1(4'b0011), .out(multiplexer_27_out), .sel(product_16bit[5]));
  Mod10_adder mod10_adder_17 (
    .Cin(mod10_adder_16_cout), .A(multiplexer_22_out), .B(mod10_adder_12_mod10_out),
    .Cout(mod10_adder_17_cout), .mod10_out(mod10_adder_17_mod10_out));
  Multiplexer #(.width(4)) multiplexer_28 (
    .in0(4'b0000), .in1(4'b0000), .out(multiplexer_28_out), .sel(product_16bit[5]));
  Mod10_adder mod10_adder_18 (
    .Cin(mod10_adder_17_cout), .A(multiplexer_23_out), .B(mod10_adder_13_mod10_out),
    .Cout(mod10_adder_18_cout), .mod10_out(mod10_adder_18_mod10_out));
  Multiplexer #(.width(4)) multiplexer_29 (
    .in0(4'b0000), .in1(4'b0000), .out(multiplexer_29_out), .sel(product_16bit[5]));
  Mod10_adder mod10_adder_19 (
    .Cin(mod10_adder_18_cout), .A(multiplexer_24_out), .B(mod10_adder_14_mod10_out),
    .Cout(mod10_adder_19_cout), .mod10_out(mod10_adder_19_mod10_out));
  Multiplexer #(.width(4)) multiplexer_30 (
    .in0(4'b0000), .in1(4'b0000), .out(multiplexer_30_out), .sel(product_16bit[5]));
  Mod10_adder mod10_adder_20 (
    .Cin(mod10_adder_19_cout), .A(multiplexer_25_out), .B(mod10_adder_15_mod10_out),
    .mod10_out(mod10_adder_20_mod10_out));  // open: Cout
  Multiplexer #(.width(4)) multiplexer_31 (
    .in0(4'b0000), .in1(4'b0100), .out(multiplexer_31_out), .sel(product_16bit[6]));
  Mod10_adder mod10_adder_21 (
    .Cin(1'b0), .A(multiplexer_26_out), .B(mod10_adder_16_mod10_out), .Cout(mod10_adder_21_cout),
    .mod10_out(mod10_adder_21_mod10_out));
  Multiplexer #(.width(4)) multiplexer_32 (
    .in0(4'b0000), .in1(4'b0110), .out(multiplexer_32_out), .sel(product_16bit[6]));
  Mod10_adder mod10_adder_22 (
    .Cin(mod10_adder_21_cout), .A(multiplexer_27_out), .B(mod10_adder_17_mod10_out),
    .Cout(mod10_adder_22_cout), .mod10_out(mod10_adder_22_mod10_out));
  Multiplexer #(.width(4)) multiplexer_33 (
    .in0(4'b0000), .in1(4'b0000), .out(multiplexer_33_out), .sel(product_16bit[6]));
  Mod10_adder mod10_adder_23 (
    .Cin(mod10_adder_22_cout), .A(multiplexer_28_out), .B(mod10_adder_18_mod10_out),
    .Cout(mod10_adder_23_cout), .mod10_out(mod10_adder_23_mod10_out));
  Multiplexer #(.width(4)) multiplexer_34 (
    .in0(4'b0000), .in1(4'b0000), .out(multiplexer_34_out), .sel(product_16bit[6]));
  Mod10_adder mod10_adder_24 (
    .Cin(mod10_adder_23_cout), .A(multiplexer_29_out), .B(mod10_adder_19_mod10_out),
    .Cout(mod10_adder_24_cout), .mod10_out(mod10_adder_24_mod10_out));
  Multiplexer #(.width(4)) multiplexer_35 (
    .in0(4'b0000), .in1(4'b0000), .out(multiplexer_35_out), .sel(product_16bit[6]));
  Mod10_adder mod10_adder_25 (
    .Cin(mod10_adder_24_cout), .A(multiplexer_30_out), .B(mod10_adder_20_mod10_out),
    .mod10_out(mod10_adder_25_mod10_out));  // open: Cout
  Mod10_adder mod10_adder_26 (
    .Cin(1'b0), .A(multiplexer_31_out), .B(mod10_adder_21_mod10_out), .Cout(mod10_adder_26_cout),
    .mod10_out(mod10_adder_26_mod10_out));
  Mod10_adder mod10_adder_27 (
    .Cin(mod10_adder_26_cout), .A(multiplexer_32_out), .B(mod10_adder_22_mod10_out),
    .Cout(mod10_adder_27_cout), .mod10_out(mod10_adder_27_mod10_out));
  Mod10_adder mod10_adder_28 (
    .Cin(mod10_adder_27_cout), .A(multiplexer_33_out), .B(mod10_adder_23_mod10_out),
    .Cout(mod10_adder_28_cout), .mod10_out(mod10_adder_28_mod10_out));
  Mod10_adder mod10_adder_29 (
    .Cin(mod10_adder_28_cout), .A(multiplexer_34_out), .B(mod10_adder_24_mod10_out),
    .Cout(mod10_adder_29_cout), .mod10_out(mod10_adder_29_mod10_out));
  Mod10_adder mod10_adder_30 (
    .Cin(mod10_adder_29_cout), .A(multiplexer_35_out), .B(mod10_adder_25_mod10_out),
    .mod10_out(mod10_adder_30_mod10_out));  // open: Cout
  Multiplexer #(.width(4)) multiplexer_36 (
    .in0(4'b0000), .in1(4'b1000), .out(multiplexer_36_out), .sel(product_16bit[7]));
  Multiplexer #(.width(4)) multiplexer_37 (
    .in0(4'b0000), .in1(4'b0010), .out(multiplexer_37_out), .sel(product_16bit[7]));
  Multiplexer #(.width(4)) multiplexer_38 (
    .in0(4'b0000), .in1(4'b0001), .out(multiplexer_38_out), .sel(product_16bit[7]));
  Multiplexer #(.width(4)) multiplexer_39 (
    .in0(4'b0000), .in1(4'b0000), .out(multiplexer_39_out), .sel(product_16bit[7]));
  Multiplexer #(.width(4)) multiplexer_40 (
    .in0(4'b0000), .in1(4'b0000), .out(multiplexer_40_out), .sel(product_16bit[7]));
  Mod10_adder mod10_adder_31 (
    .Cin(1'b0), .A(multiplexer_36_out), .B(mod10_adder_26_mod10_out), .Cout(mod10_adder_31_cout),
    .mod10_out(mod10_adder_31_mod10_out));
  Mod10_adder mod10_adder_32 (
    .Cin(mod10_adder_31_cout), .A(multiplexer_37_out), .B(mod10_adder_27_mod10_out),
    .Cout(mod10_adder_32_cout), .mod10_out(mod10_adder_32_mod10_out));
  Mod10_adder mod10_adder_33 (
    .Cin(mod10_adder_32_cout), .A(multiplexer_38_out), .B(mod10_adder_28_mod10_out),
    .Cout(mod10_adder_33_cout), .mod10_out(mod10_adder_33_mod10_out));
  Mod10_adder mod10_adder_34 (
    .Cin(mod10_adder_33_cout), .A(multiplexer_39_out), .B(mod10_adder_29_mod10_out),
    .Cout(mod10_adder_34_cout), .mod10_out(mod10_adder_34_mod10_out));
  Mod10_adder mod10_adder_35 (
    .Cin(mod10_adder_34_cout), .A(multiplexer_40_out), .B(mod10_adder_30_mod10_out),
    .mod10_out(mod10_adder_35_mod10_out));  // open: Cout
  Multiplexer #(.width(4)) multiplexer_41 (
    .in0(4'b0000), .in1(4'b0110), .out(multiplexer_41_out), .sel(product_16bit[8]));
  Multiplexer #(.width(4)) multiplexer_42 (
    .in0(4'b0000), .in1(4'b0101), .out(multiplexer_42_out), .sel(product_16bit[8]));
  Multiplexer #(.width(4)) multiplexer_43 (
    .in0(4'b0000), .in1(4'b0010), .out(multiplexer_43_out), .sel(product_16bit[8]));
  Multiplexer #(.width(4)) multiplexer_44 (
    .in0(4'b0000), .in1(4'b0000), .out(multiplexer_44_out), .sel(product_16bit[8]));
  Multiplexer #(.width(4)) multiplexer_45 (
    .in0(4'b0000), .in1(4'b0000), .out(multiplexer_45_out), .sel(product_16bit[8]));
  Mod10_adder mod10_adder_36 (
    .Cin(1'b0), .A(multiplexer_41_out), .B(mod10_adder_31_mod10_out), .Cout(mod10_adder_36_cout),
    .mod10_out(mod10_adder_36_mod10_out));
  Mod10_adder mod10_adder_37 (
    .Cin(mod10_adder_36_cout), .A(multiplexer_42_out), .B(mod10_adder_32_mod10_out),
    .Cout(mod10_adder_37_cout), .mod10_out(mod10_adder_37_mod10_out));
  Mod10_adder mod10_adder_38 (
    .Cin(mod10_adder_37_cout), .A(multiplexer_43_out), .B(mod10_adder_33_mod10_out),
    .Cout(mod10_adder_38_cout), .mod10_out(mod10_adder_38_mod10_out));
  Mod10_adder mod10_adder_39 (
    .Cin(mod10_adder_38_cout), .A(multiplexer_44_out), .B(mod10_adder_34_mod10_out),
    .Cout(mod10_adder_39_cout), .mod10_out(mod10_adder_39_mod10_out));
  Mod10_adder mod10_adder_40 (
    .Cin(mod10_adder_39_cout), .A(multiplexer_45_out), .B(mod10_adder_35_mod10_out),
    .mod10_out(mod10_adder_40_mod10_out));  // open: Cout
  Multiplexer #(.width(4)) multiplexer_46 (
    .in0(4'b0000), .in1(4'b0010), .out(multiplexer_46_out), .sel(product_16bit[9]));
  Multiplexer #(.width(4)) multiplexer_47 (
    .in0(4'b0000), .in1(4'b0001), .out(multiplexer_47_out), .sel(product_16bit[9]));
  Multiplexer #(.width(4)) multiplexer_48 (
    .in0(4'b0000), .in1(4'b0101), .out(multiplexer_48_out), .sel(product_16bit[9]));
  Multiplexer #(.width(4)) multiplexer_49 (
    .in0(4'b0000), .in1(4'b0000), .out(multiplexer_49_out), .sel(product_16bit[9]));
  Multiplexer #(.width(4)) multiplexer_50 (
    .in0(4'b0000), .in1(4'b0000), .out(multiplexer_50_out), .sel(product_16bit[9]));
  Mod10_adder mod10_adder_41 (
    .Cin(1'b0), .A(multiplexer_46_out), .B(mod10_adder_36_mod10_out), .Cout(mod10_adder_41_cout),
    .mod10_out(mod10_adder_41_mod10_out));
  Mod10_adder mod10_adder_42 (
    .Cin(mod10_adder_41_cout), .A(multiplexer_47_out), .B(mod10_adder_37_mod10_out),
    .Cout(mod10_adder_42_cout), .mod10_out(mod10_adder_42_mod10_out));
  Mod10_adder mod10_adder_43 (
    .Cin(mod10_adder_42_cout), .A(multiplexer_48_out), .B(mod10_adder_38_mod10_out),
    .Cout(mod10_adder_43_cout), .mod10_out(mod10_adder_43_mod10_out));
  Mod10_adder mod10_adder_44 (
    .Cin(mod10_adder_43_cout), .A(multiplexer_49_out), .B(mod10_adder_39_mod10_out),
    .Cout(mod10_adder_44_cout), .mod10_out(mod10_adder_44_mod10_out));
  Mod10_adder mod10_adder_45 (
    .Cin(mod10_adder_44_cout), .A(multiplexer_50_out), .B(mod10_adder_40_mod10_out),
    .mod10_out(mod10_adder_45_mod10_out));  // open: Cout
  Multiplexer #(.width(4)) multiplexer_51 (
    .in0(4'b0000), .in1(4'b0100), .out(multiplexer_51_out), .sel(product_16bit[10]));
  Multiplexer #(.width(4)) multiplexer_52 (
    .in0(4'b0000), .in1(4'b0010), .out(multiplexer_52_out), .sel(product_16bit[10]));
  Multiplexer #(.width(4)) multiplexer_53 (
    .in0(4'b0000), .in1(4'b0000), .out(multiplexer_53_out), .sel(product_16bit[10]));
  Multiplexer #(.width(4)) multiplexer_54 (
    .in0(4'b0000), .in1(4'b0001), .out(multiplexer_54_out), .sel(product_16bit[10]));
  Multiplexer #(.width(4)) multiplexer_55 (
    .in0(4'b0000), .in1(4'b0000), .out(multiplexer_55_out), .sel(product_16bit[10]));
  Mod10_adder mod10_adder_46 (
    .Cin(1'b0), .A(multiplexer_51_out), .B(mod10_adder_41_mod10_out), .Cout(mod10_adder_46_cout),
    .mod10_out(mod10_adder_46_mod10_out));
  Mod10_adder mod10_adder_47 (
    .Cin(mod10_adder_46_cout), .A(multiplexer_52_out), .B(mod10_adder_42_mod10_out),
    .Cout(mod10_adder_47_cout), .mod10_out(mod10_adder_47_mod10_out));
  Mod10_adder mod10_adder_48 (
    .Cin(mod10_adder_47_cout), .A(multiplexer_53_out), .B(mod10_adder_43_mod10_out),
    .Cout(mod10_adder_48_cout), .mod10_out(mod10_adder_48_mod10_out));
  Mod10_adder mod10_adder_49 (
    .Cin(mod10_adder_48_cout), .A(multiplexer_54_out), .B(mod10_adder_44_mod10_out),
    .Cout(mod10_adder_49_cout), .mod10_out(mod10_adder_49_mod10_out));
  Mod10_adder mod10_adder_50 (
    .Cin(mod10_adder_49_cout), .A(multiplexer_55_out), .B(mod10_adder_45_mod10_out),
    .mod10_out(mod10_adder_50_mod10_out));  // open: Cout
  Multiplexer #(.width(4)) multiplexer_56 (
    .in0(4'b0000), .in1(4'b1000), .out(multiplexer_56_out), .sel(product_16bit[11]));
  Multiplexer #(.width(4)) multiplexer_57 (
    .in0(4'b0000), .in1(4'b0100), .out(multiplexer_57_out), .sel(product_16bit[11]));
  Multiplexer #(.width(4)) multiplexer_58 (
    .in0(4'b0000), .in1(4'b0000), .out(multiplexer_58_out), .sel(product_16bit[11]));
  Multiplexer #(.width(4)) multiplexer_59 (
    .in0(4'b0000), .in1(4'b0010), .out(multiplexer_59_out), .sel(product_16bit[11]));
  Multiplexer #(.width(4)) multiplexer_60 (
    .in0(4'b0000), .in1(4'b0000), .out(multiplexer_60_out), .sel(product_16bit[11]));
  Multiplexer #(.width(4)) multiplexer_61 (
    .in0(4'b0000), .in1(4'b0110), .out(multiplexer_61_out), .sel(product_16bit[12]));
  Mod10_adder mod10_adder_51 (
    .Cin(1'b0), .A(multiplexer_56_out), .B(mod10_adder_46_mod10_out), .Cout(mod10_adder_51_cout),
    .mod10_out(mod10_adder_51_mod10_out));
  Multiplexer #(.width(4)) multiplexer_62 (
    .in0(4'b0000), .in1(4'b1001), .out(multiplexer_62_out), .sel(product_16bit[12]));
  Mod10_adder mod10_adder_52 (
    .Cin(mod10_adder_51_cout), .A(multiplexer_57_out), .B(mod10_adder_47_mod10_out),
    .Cout(mod10_adder_52_cout), .mod10_out(mod10_adder_52_mod10_out));
  Multiplexer #(.width(4)) multiplexer_63 (
    .in0(4'b0000), .in1(4'b0000), .out(multiplexer_63_out), .sel(product_16bit[12]));
  Mod10_adder mod10_adder_53 (
    .Cin(mod10_adder_52_cout), .A(multiplexer_58_out), .B(mod10_adder_48_mod10_out),
    .Cout(mod10_adder_53_cout), .mod10_out(mod10_adder_53_mod10_out));
  Multiplexer #(.width(4)) multiplexer_64 (
    .in0(4'b0000), .in1(4'b0100), .out(multiplexer_64_out), .sel(product_16bit[12]));
  Mod10_adder mod10_adder_54 (
    .Cin(mod10_adder_53_cout), .A(multiplexer_59_out), .B(mod10_adder_49_mod10_out),
    .Cout(mod10_adder_54_cout), .mod10_out(mod10_adder_54_mod10_out));
  Multiplexer #(.width(4)) multiplexer_65 (
    .in0(4'b0000), .in1(4'b0000), .out(multiplexer_65_out), .sel(product_16bit[12]));
  Mod10_adder mod10_adder_55 (
    .Cin(mod10_adder_54_cout), .A(multiplexer_60_out), .B(mod10_adder_50_mod10_out),
    .mod10_out(mod10_adder_55_mod10_out));  // open: Cout
  Multiplexer #(.width(4)) multiplexer_66 (
    .in0(4'b0000), .in1(4'b0010), .out(multiplexer_66_out), .sel(product_16bit[13]));
  Mod10_adder mod10_adder_56 (
    .Cin(1'b0), .A(multiplexer_61_out), .B(mod10_adder_51_mod10_out), .Cout(mod10_adder_56_cout),
    .mod10_out(mod10_adder_56_mod10_out));
  Multiplexer #(.width(4)) multiplexer_67 (
    .in0(4'b0000), .in1(4'b1001), .out(multiplexer_67_out), .sel(product_16bit[13]));
  Mod10_adder mod10_adder_57 (
    .Cin(mod10_adder_56_cout), .A(multiplexer_62_out), .B(mod10_adder_52_mod10_out),
    .Cout(mod10_adder_57_cout), .mod10_out(mod10_adder_57_mod10_out));
  Multiplexer #(.width(4)) multiplexer_68 (
    .in0(4'b0000), .in1(4'b0001), .out(multiplexer_68_out), .sel(product_16bit[13]));
  Mod10_adder mod10_adder_58 (
    .Cin(mod10_adder_57_cout), .A(multiplexer_63_out), .B(mod10_adder_53_mod10_out),
    .Cout(mod10_adder_58_cout), .mod10_out(mod10_adder_58_mod10_out));
  Multiplexer #(.width(4)) multiplexer_69 (
    .in0(4'b0000), .in1(4'b1000), .out(multiplexer_69_out), .sel(product_16bit[13]));
  Mod10_adder mod10_adder_59 (
    .Cin(mod10_adder_58_cout), .A(multiplexer_64_out), .B(mod10_adder_54_mod10_out),
    .Cout(mod10_adder_59_cout), .mod10_out(mod10_adder_59_mod10_out));
  Multiplexer #(.width(4)) multiplexer_70 (
    .in0(4'b0000), .in1(4'b0000), .out(multiplexer_70_out), .sel(product_16bit[13]));
  Mod10_adder mod10_adder_60 (
    .Cin(mod10_adder_59_cout), .A(multiplexer_65_out), .B(mod10_adder_55_mod10_out),
    .mod10_out(mod10_adder_60_mod10_out));  // open: Cout
  Multiplexer #(.width(4)) multiplexer_71 (
    .in0(4'b0000), .in1(4'b0100), .out(multiplexer_71_out), .sel(product_16bit[14]));
  Mod10_adder mod10_adder_61 (
    .Cin(1'b0), .A(multiplexer_66_out), .B(mod10_adder_56_mod10_out), .Cout(mod10_adder_61_cout),
    .mod10_out(mod10_adder_61_mod10_out));
  Multiplexer #(.width(4)) multiplexer_72 (
    .in0(4'b0000), .in1(4'b1000), .out(multiplexer_72_out), .sel(product_16bit[14]));
  Mod10_adder mod10_adder_62 (
    .Cin(mod10_adder_61_cout), .A(multiplexer_67_out), .B(mod10_adder_57_mod10_out),
    .Cout(mod10_adder_62_cout), .mod10_out(mod10_adder_62_mod10_out));
  Multiplexer #(.width(4)) multiplexer_73 (
    .in0(4'b0000), .in1(4'b0011), .out(multiplexer_73_out), .sel(product_16bit[14]));
  Mod10_adder mod10_adder_63 (
    .Cin(mod10_adder_62_cout), .A(multiplexer_68_out), .B(mod10_adder_58_mod10_out),
    .Cout(mod10_adder_63_cout), .mod10_out(mod10_adder_63_mod10_out));
  Multiplexer #(.width(4)) multiplexer_74 (
    .in0(4'b0000), .in1(4'b0110), .out(multiplexer_74_out), .sel(product_16bit[14]));
  Mod10_adder mod10_adder_64 (
    .Cin(mod10_adder_63_cout), .A(multiplexer_69_out), .B(mod10_adder_59_mod10_out),
    .Cout(mod10_adder_64_cout), .mod10_out(mod10_adder_64_mod10_out));
  Multiplexer #(.width(4)) multiplexer_75 (
    .in0(4'b0000), .in1(4'b0001), .out(multiplexer_75_out), .sel(product_16bit[14]));
  Mod10_adder mod10_adder_65 (
    .Cin(mod10_adder_64_cout), .A(multiplexer_70_out), .B(mod10_adder_60_mod10_out),
    .mod10_out(mod10_adder_65_mod10_out));  // open: Cout
  Mod10_adder mod10_adder_66 (
    .Cin(1'b0), .A(multiplexer_71_out), .B(mod10_adder_61_mod10_out), .Cout(mod10_adder_66_cout),
    .mod10_out(mod10_adder_66_mod10_out));
  Mod10_adder mod10_adder_67 (
    .Cin(mod10_adder_66_cout), .A(multiplexer_72_out), .B(mod10_adder_62_mod10_out),
    .Cout(mod10_adder_67_cout), .mod10_out(mod10_adder_67_mod10_out));
  Mod10_adder mod10_adder_68 (
    .Cin(mod10_adder_67_cout), .A(multiplexer_73_out), .B(mod10_adder_63_mod10_out),
    .Cout(mod10_adder_68_cout), .mod10_out(mod10_adder_68_mod10_out));
  Mod10_adder mod10_adder_69 (
    .Cin(mod10_adder_68_cout), .A(multiplexer_74_out), .B(mod10_adder_64_mod10_out),
    .Cout(mod10_adder_69_cout), .mod10_out(mod10_adder_69_mod10_out));
  Mod10_adder mod10_adder_70 (
    .Cin(mod10_adder_69_cout), .A(multiplexer_75_out), .B(mod10_adder_65_mod10_out),
    .mod10_out(mod10_adder_70_mod10_out));  // open: Cout
  Multiplexer #(.width(4)) multiplexer_76 (
    .in0(4'b0000), .in1(4'b1000), .out(multiplexer_76_out), .sel(product_16bit[15]));
  Multiplexer #(.width(4)) multiplexer_77 (
    .in0(4'b0000), .in1(4'b0110), .out(multiplexer_77_out), .sel(product_16bit[15]));
  Multiplexer #(.width(4)) multiplexer_78 (
    .in0(4'b0000), .in1(4'b0111), .out(multiplexer_78_out), .sel(product_16bit[15]));
  Multiplexer #(.width(4)) multiplexer_79 (
    .in0(4'b0000), .in1(4'b0010), .out(multiplexer_79_out), .sel(product_16bit[15]));
  Multiplexer #(.width(4)) multiplexer_80 (
    .in0(4'b0000), .in1(4'b0011), .out(multiplexer_80_out), .sel(product_16bit[15]));
  Mod10_adder mod10_adder_71 (
    .Cin(1'b0), .A(multiplexer_76_out), .B(mod10_adder_66_mod10_out), .Cout(mod10_adder_71_cout),
    .mod10_out(digit_1));
  Mod10_adder mod10_adder_72 (
    .Cin(mod10_adder_71_cout), .A(multiplexer_77_out), .B(mod10_adder_67_mod10_out),
    .Cout(mod10_adder_72_cout), .mod10_out(digit_2));
  Mod10_adder mod10_adder_73 (
    .Cin(mod10_adder_72_cout), .A(multiplexer_78_out), .B(mod10_adder_68_mod10_out),
    .Cout(mod10_adder_73_cout), .mod10_out(digit_3));
  Mod10_adder mod10_adder_74 (
    .Cin(mod10_adder_73_cout), .A(multiplexer_79_out), .B(mod10_adder_69_mod10_out),
    .Cout(mod10_adder_74_cout), .mod10_out(digit_4));
  Mod10_adder mod10_adder_75 (
    .Cin(mod10_adder_74_cout), .A(multiplexer_80_out), .B(mod10_adder_70_mod10_out), .mod10_out(digit_5));  // open: Cout
endmodule
